// Logisim project 1.circ as structural Verilog: 1 circuit, main circuit main
module main (
  input  in_1,
  input  in_2,
  input  in_3,
  input  in_4
);

  wire and_1_out, and_2_out, not_1_out, or_1_out, xor_1_out;

  and and_1 (and_1_out, in_1, in_2);
  LED led_1 (.in(or_1_out));
  or or_1 (or_1_out, and_1_out, and_2_out);
  not not_1 (not_1_out, in_1);
  and and_2 (and_2_out, not_1_out, xor_1_out);
  xor xor_1 (xor_1_out, in_3, in_4);

  // Notes on the sheet:
  //         A        B        C        D
endmodule
